// Digital circuit DMux.dig as structural Verilog
module DMux (
  input  in,
  input  sel,
  output a,
  output b
);

  wire not_1_out;

  not not_1 (not_1_out, sel);
  and and_1 (a, not_1_out, in);
  and and_2 (b, in, sel);
endmodule
