// Digital circuit DMux4Way.dig as structural Verilog
module DMux4Way (
  input  in_5,
  input  sel1,
  input  sel2,
  output out_1,
  output out_2,
  output out_3,
  output out_4
);

  wire demultiplexer_1_out_0, demultiplexer_1_out_1;

  Demultiplexer demultiplexer_1 (.sel(sel1), .in(in_5), .out_0(demultiplexer_1_out_0), .out_1(demultiplexer_1_out_1));
  Demultiplexer demultiplexer_2 (.sel(sel2), .in(demultiplexer_1_out_0), .out_0(out_1), .out_1(out_2));
  Demultiplexer demultiplexer_3 (.sel(sel2), .in(demultiplexer_1_out_1), .out_0(out_3), .out_1(out_4));
endmodule
