// Digital circuit halfAdder.dig as structural Verilog
module halfAdder (
  input  in_1,
  input  in_2,
  output sum,
  output carry
);

  xor xor_1 (sum, in_1, in_2);
  and and_1 (carry, in_1, in_2);
endmodule
